// Logisim project ALU.circ as structural Verilog: 2 circuits, main circuit ALU
module ALU (
  input  [31:0] A,
  input  [31:0] B,
  input  [4:0] Shift,
  input  [3:0] Codop,
  input  CarryIn,
  output [3:0] Flags,
  output [31:0] S
);

  wire ADC_C, ADC_V, and_4_out, and_5_out, and_6_out, and_7_out, and_8_out, and_9_out, and_10_out,
       and_11_out, ASR_C, CMN_C, CMN_V, CMP_C, CMP_V, LSL_C, LSR_C, not_1_out, not_6_out, not_7_out,
       not_8_out, not_9_out, not_10_out, not_11_out, not_12_out, not_13_out, not_14_out, not_15_out,
       not_16_out, not_17_out, not_18_out, not_19_out, ROR_C, RSB_V, SBC_C, SBC_V, subtractor_1_bout,
       subtractor_3_bout;
  wire [4:0] adder_1_out, subtractor_4_out, subtractor_5_out, xor_2_out;
  wire [30:0] shifter_3_out;
  wire [31:0] adder_2_out, and_2_out, and_3_out, CMN_NV, CMP_NV, multiplexer_2_out, multiplier_1_out,
       not_4_out, not_5_out, or_1_out, shifter_1_out, shifter_2_out, shifter_4_out, subtractor_1_out,
       subtractor_2_out, TST_NV, xor_1_out;

  assign xor_1_out = A ^ B;  // XOR_Gate xor_1, 32 bits wide
  assign xor_2_out = {5{1'b1}} ^ Shift;  // XOR_Gate xor_2, 5 bits wide
  Adder #(.width(5)) adder_1 (.a(xor_2_out), .b(5'b00001), .out(adder_1_out));  // open: cin, cout
  Shifter #(.width(32)) shifter_1 (.in(B), .\dist (Shift), .out(shifter_1_out));
  Shifter #(.shift("lr"), .width(32)) shifter_2 (.in(B), .\dist (Shift), .out(shifter_2_out));
  Adder #(.width(32)) adder_2 (.a(A), .b(B), .out(adder_2_out), .cin(CarryIn), .cout(ADC_C));
  not not_1 (not_1_out, CarryIn);
  Subtractor #(.width(32)) subtractor_1 (
    .a(B), .b(A), .out(subtractor_1_out), .bin(not_1_out), .bout(subtractor_1_bout));
  not not_2 (SBC_C, subtractor_1_bout);
  Shifter #(.shift("rr"), .width(32)) shifter_3 (.in(B), .\dist (Shift), .out({ROR_C, shifter_3_out}));
  assign TST_NV = A & B;  // AND_Gate and_1, 32 bits wide
  Subtractor #(.width(32)) subtractor_2 (.a({32{1'b0}}), .b(A), .out(subtractor_2_out));  // open: bin, bout
  Comparator #(.width(32)) comparator_1 (.a(A), .b(32'h80000000), .eq(RSB_V));  // open: gt, lt
  Subtractor #(.width(32)) subtractor_3 (.a(B), .b(A), .out(CMP_NV), .bout(subtractor_3_bout));  // open: bin
  not not_3 (CMP_C, subtractor_3_bout);
  Adder #(.width(32)) adder_3 (.a(B), .b(A), .out(CMN_NV), .cout(CMN_C));  // open: cin
  assign or_1_out = A | B;  // OR_Gate or_1, 32 bits wide
  Multiplier #(.mode("twosComplement"), .width(32)) multiplier_1 (
    .a(A), .b(B), .out(multiplier_1_out));  // open: cin, cout
  assign not_4_out = ~A;  // NOT_Gate not_4, 32 bits wide
  assign not_5_out = ~A;  // NOT_Gate not_5, 32 bits wide
  assign and_2_out = A & B;  // AND_Gate and_2, 32 bits wide
  BitSelector #(.width(32)) bitselector_1 (.in(B), .out(LSL_C), .sel(adder_1_out));
  Subtractor #(.width(5)) subtractor_4 (.a(Shift), .b(5'b00001), .out(subtractor_4_out));  // open: bin, bout
  BitSelector #(.width(32)) bitselector_2 (.in(B), .out(LSR_C), .sel(subtractor_4_out));
  Subtractor #(.width(5)) subtractor_5 (.a(Shift), .b(5'b00001), .out(subtractor_5_out));  // open: bin, bout
  Shifter #(.shift("ar"), .width(32)) shifter_4 (.in(B), .\dist (Shift), .out(shifter_4_out));
  assign and_3_out = not_4_out & B;  // AND_Gate and_3, 32 bits wide
  BitSelector #(.width(32)) bitselector_3 (.in(B), .out(ASR_C), .sel(subtractor_5_out));
  Multiplexer #(.select(4), .width(32)) multiplexer_1 (
    .in0(and_2_out), .in1(xor_1_out), .in2(shifter_1_out), .in3(shifter_2_out), .in4(shifter_4_out),
    .in5(adder_2_out), .in6(subtractor_1_out), .in7({ROR_C, shifter_3_out}), .in8(B), .in9(subtractor_2_out),
    .in10(B), .in11(B), .in12(or_1_out), .in13(multiplier_1_out), .in14(and_3_out), .in15(not_5_out),
    .out(S), .sel(Codop));
  not not_6 (not_6_out, A[31]);
  not not_7 (not_7_out, adder_2_out[31]);
  not not_8 (not_8_out, A[31]);
  not not_9 (not_9_out, B[31]);
  not not_10 (not_10_out, A[31]);
  not not_11 (not_11_out, CMP_NV[31]);
  not not_12 (not_12_out, not_6_out);
  not not_13 (not_13_out, B[31]);
  not not_14 (not_14_out, CMN_NV[31]);
  not not_15 (not_15_out, A[31]);
  not not_16 (not_16_out, B[31]);
  Multiplexer #(.select(4), .width(32)) multiplexer_2 (
    .in0(S), .in1(S), .in2(S), .in3(S), .in4(S), .in5(S), .in6(S), .in7(S), .in8(TST_NV), .in9(S),
    .in10(CMP_NV), .in11(CMN_NV), .in12(S), .in13(S), .in14(S), .in15(S), .out(multiplexer_2_out), .sel(Codop));
  and and_4 (and_4_out, not_7_out, A[31], B[31]);
  and and_5 (and_5_out, adder_2_out[31], not_8_out, not_9_out);
  or or_2 (ADC_V, and_4_out, and_5_out);
  not not_17 (not_17_out, subtractor_1_out[31]);
  not not_18 (not_18_out, not_10_out);
  not not_19 (not_19_out, B[31]);
  and and_6 (and_6_out, not_11_out, not_6_out, B[31]);
  and and_7 (and_7_out, CMP_NV[31], not_12_out, not_13_out);
  and and_8 (and_8_out, not_14_out, A[31], B[31]);
  and and_9 (and_9_out, CMN_NV[31], not_15_out, not_16_out);
  and and_10 (and_10_out, not_17_out, not_10_out, B[31]);
  and and_11 (and_11_out, subtractor_1_out[31], not_18_out, not_19_out);
  or or_3 (CMP_V, and_6_out, and_7_out);
  or or_4 (CMN_V, and_8_out, and_9_out);
  Comparator #(.width(32)) comparator_2 (
    .a(multiplexer_2_out), .b({32{1'b0}}), .eq(Flags[2]), .lt(Flags[3]));  // open: gt
  or or_5 (SBC_V, and_10_out, and_11_out);
  Multiplexer #(.select(4), .width(2)) multiplexer_3 (
    .in0(2'b00), .in1(2'b00), .in2({1'b0, LSL_C}), .in3({1'b0, LSR_C}), .in4({1'b0, ASR_C}),
    .in5({ADC_V, ADC_C}), .in6({SBC_V, SBC_C}), .in7({1'b0, ROR_C}), .in8(2'b00), .in9({RSB_V, 1'b0}),
    .in10({CMP_V, CMP_C}), .in11({CMN_V, CMN_C}), .in12(2'b00), .in13(2'b00), .in14(2'b00), .in15(2'b00),
    .out({Flags[0], Flags[1]}), .sel(Codop));

  // Other names for the same wires on the sheet: Z = Flags[2]; N = Flags[3]

  // Notes on the sheet:
  //   Note: for ROR, C = N
  //   Note 2: assume that shift > 0 for LSL and LSR
  //   left shift
  //   right shift
  //   A + B + Cin
  //   B - A + not Cin
  //   rot right shift
  //   AND
  //   0 - A
  //   B - A
  //   A + B
  //   A or B
  //   AND
  //   XOR
  //   arith right shift
endmodule

module test (
  input  S,
  input  B,
  input  A,
  output Overflow
);

  wire and_1_out, and_2_out, not_1_out, not_2_out, not_3_out;

  not not_1 (not_1_out, S);
  not not_2 (not_2_out, B);
  not not_3 (not_3_out, A);
  and and_1 (and_1_out, not_1_out, not_2_out, A);
  or or_1 (Overflow, and_1_out, and_2_out);
  and and_2 (and_2_out, S, B, not_3_out);
endmodule
