// Logisim project Ctl_Conditional.circ as structural Verilog: 1 circuit, main circuit Conditional
module Conditional (
  input  Enable,
  input  [15:0] Instruction,
  input  Z,
  input  C,
  input  N,
  input  V,
  output [10:0] Offset,
  output Verified
);

  wire and_1_out, and_2_out, comparator_1_eq, multiplexer_1_out, multiplexer_3_out, not_1_out, not_2_out,
       not_3_out, not_4_out, not_5_out, not_6_out, or_1_out, or_2_out;
  wire [10:0] bit_extender_1_out, multiplexer_2_out;

  not not_1 (not_1_out, 1'b1);
  not not_2 (not_2_out, Z);
  not not_3 (not_3_out, C);
  not not_4 (not_4_out, N);
  not not_5 (not_5_out, V);
  and and_1 (and_1_out, not_2_out, C);
  or or_1 (or_1_out, Z, not_3_out);
  Comparator #(.width(1)) comparator_1 (.a(N), .b(V), .eq(comparator_1_eq));  // open: gt, lt
  not not_6 (not_6_out, comparator_1_eq);
  and and_2 (and_2_out, comparator_1_eq, not_2_out);
  or or_2 (or_2_out, not_6_out, Z);
  Multiplexer #(.select(4)) multiplexer_1 (
    .in0(Z), .in1(not_2_out), .in2(C), .in3(not_3_out), .in4(N), .in5(not_4_out), .in6(V), .in7(not_5_out),
    .in8(and_1_out), .in9(or_1_out), .in10(comparator_1_eq), .in11(not_6_out), .in12(and_2_out),
    .in13(or_2_out), .in14(1'b1), .in15(not_1_out), .out(multiplexer_1_out), .sel(Instruction[11:8]));
  assign bit_extender_1_out = {{3{Instruction[7]}}, Instruction[7:0]};  // Bit_Extender bit_extender_1
  Multiplexer #(.width(11)) multiplexer_2 (
    .in0(bit_extender_1_out), .in1(Instruction[10:0]), .out(multiplexer_2_out), .sel(Instruction[13]));
  Multiplexer multiplexer_3 (.in0(multiplexer_1_out), .in1(1'b1), .out(multiplexer_3_out), .sel(Instruction[13]));
  Multiplexer #(.width(11)) multiplexer_4 (.in0({11{1'b0}}), .in1(multiplexer_2_out), .out(Offset), .sel(Enable));
  and and_3 (Verified, multiplexer_3_out, Enable);

  // Other names for the same wires on the sheet: E = Enable; FLAGS[3:0] = {V, N, C, Z}; imm8[7:0] = Instruction[7:0];
  //   imm11[10:0] = Instruction[10:0]; cond[3:0] = Instruction[11:8]; bit_13 = Instruction[13]
endmodule
