// Logisim project Ctl_Load_Store.circ as structural Verilog: 1 circuit, main circuit Load_Store
module Load_Store (
  input  [15:0] Instruction,
  input  Clk,
  input  Reset,
  input  Enable,
  input  [31:0] Stack_Pointer,
  output [2:0] Rmd,
  output [31:0] RAM_Addr,
  output PC_Hold,
  output Store,
  output Load
);

  wire and_1_out, and_2_out, not_1_out, Pc_Hold_t, Store_t;
  wire [31:0] adder_1_out, Offset;

  and and_1 (and_1_out, Instruction[11], not_1_out);
  not not_1 (not_1_out, Pc_Hold_t);
  D_Flip_Flop d_ff_1 (.D(and_1_out), .clk(Clk), .Q(Pc_Hold_t), .reset(Reset));  // open: Qn, preset
  assign Offset = {{24{Instruction[7]}}, Instruction[7:0]};  // Bit_Extender bit_extender_1
  not not_2 (Store_t, Instruction[11]);
  Adder #(.width(32)) adder_1 (.a(Stack_Pointer), .b(Offset), .out(adder_1_out));  // open: cin, cout
  and and_2 (and_2_out, Pc_Hold_t, Instruction[11]);
  Multiplexer multiplexer_1 (.in0(1'b0), .in1(and_2_out), .out(PC_Hold), .sel(Enable));
  Multiplexer multiplexer_2 (.in0(1'b0), .in1(Store_t), .out(Store), .sel(Enable));
  Multiplexer multiplexer_3 (.in0(1'b0), .in1(Instruction[11]), .out(Load), .sel(Enable));
  Multiplexer #(.width(3)) multiplexer_4 (.in0(3'b000), .in1(Instruction[10:8]), .out(Rmd), .sel(Enable));
  Multiplexer #(.width(32)) multiplexer_5 (.in0({32{1'b0}}), .in1(adder_1_out), .out(RAM_Addr), .sel(Enable));

  // Other names for the same wires on the sheet: E = Enable; Rmd_t[2:0] = Instruction[10:8]; Load_t = Instruction[11]

  // Notes on the sheet:
  //   Instruction: pull=down
  //   Delay load and hold PC for 1 cycle for the RAM to send out requested data 
endmodule
