// Logisim project Ctl_Shift_Add_Sub_Mov.circ as structural Verilog: 2 circuits, main circuit Shift_Add_Sub_Mov
module Shift_Add_Sub_Mov (
  input  [15:0] Instruction,
  input  Enable,
  output [31:0] Imm32,
  output Imm32_Enable,
  output [2:0] Rm,
  output [3:0] Flags_Update_Mask,
  output [2:0] Rn,
  output [3:0] ALU_Opcode,
  output Carry,
  output [2:0] Rd,
  output [4:0] Imm5
);

  wire and_1_out, comparator_1_eq, comparator_2_gt, comparator_3_lt;
  wire [2:0] multiplexer_6_out, multiplexer_7_out, multiplexer_8_out;
  wire [3:0] Codop, Flags;
  wire [4:0] Choice, multiplexer_9_out;
  wire [31:0] bit_extender_1_out, bit_extender_2_out, bit_extender_3_out, multiplexer_5_out, negator_1_out;

  Comparator #(.width(4)) comparator_1 (.a(Codop), .b(4'b0110), .eq(comparator_1_eq));  // open: gt, lt
  Multiplexer #(.width(4)) multiplexer_1 (.in0(4'b0000), .in1(Flags), .out(Flags_Update_Mask), .sel(Enable));
  Multiplexer #(.width(4)) multiplexer_2 (.in0(4'b0000), .in1(Codop), .out(ALU_Opcode), .sel(Enable));
  Multiplexer multiplexer_3 (.in0(1'b0), .in1(comparator_1_eq), .out(Carry), .sel(Enable));
  getter getter_1 (.E(Instruction[13:9]), .Choice(Choice), .Codop(Codop), .Flags(Flags));
  Comparator #(.width(5)) comparator_2 (.a(Choice), .b(5'b00100), .gt(comparator_2_gt));  // open: eq, lt
  Comparator #(.width(5)) comparator_3 (.a(Choice), .b(5'b01011), .lt(comparator_3_lt));  // open: gt, eq
  Multiplexer multiplexer_4 (.in0(1'b0), .in1(and_1_out), .out(Imm32_Enable), .sel(Enable));
  and and_1 (and_1_out, comparator_3_lt, comparator_2_gt);
  assign bit_extender_1_out = {{24{Instruction[7]}}, Instruction[7:0]};  // Bit_Extender bit_extender_1
  Negator #(.width(32)) negator_1 (.in(bit_extender_1_out), .out(negator_1_out));
  assign bit_extender_2_out = {{24{Instruction[7]}}, Instruction[7:0]};  // Bit_Extender bit_extender_2
  assign bit_extender_3_out = {{29{Instruction[8]}}, Instruction[8:6]};  // Bit_Extender bit_extender_3
  Multiplexer #(.select(5), .width(32)) multiplexer_5 (
    .in0({32{1'b0}}), .in1({32{1'b0}}), .in2({32{1'b0}}), .in3({32{1'b0}}), .in4({32{1'b0}}),
    .in5(bit_extender_3_out), .in6(bit_extender_3_out), .in7(negator_1_out), .in8(bit_extender_2_out),
    .in9(bit_extender_2_out), .in10(bit_extender_2_out), .in11({32{1'b0}}), .in12({32{1'b0}}),
    .in13({32{1'b0}}), .in14({32{1'b0}}), .in15({32{1'b0}}), .in16({32{1'b0}}), .in17({32{1'b0}}),
    .in18({32{1'b0}}), .in19({32{1'b0}}), .in20({32{1'b0}}), .in21({32{1'b0}}), .in22({32{1'b0}}),
    .in23({32{1'b0}}), .in24({32{1'b0}}), .in25({32{1'b0}}), .in26({32{1'b0}}), .in27({32{1'b0}}),
    .in28({32{1'b0}}), .in29({32{1'b0}}), .in30({32{1'b0}}), .in31({32{1'b0}}), .out(multiplexer_5_out),
    .sel(Choice));
  Multiplexer #(.select(5), .width(3)) multiplexer_6 (
    .in0(3'b000), .in1(3'b000), .in2(3'b000), .in3(Instruction[8:6]), .in4(Instruction[8:6]), .in5(3'b000),
    .in6(3'b000), .in7(3'b000), .in8(3'b000), .in9(3'b000), .in10(3'b000), .in11(3'b000), .in12(3'b000),
    .in13(3'b000), .in14(3'b000), .in15(3'b000), .in16(3'b000), .in17(3'b000), .in18(3'b000), .in19(3'b000),
    .in20(3'b000), .in21(3'b000), .in22(3'b000), .in23(3'b000), .in24(3'b000), .in25(3'b000), .in26(3'b000),
    .in27(3'b000), .in28(3'b000), .in29(3'b000), .in30(3'b000), .in31(3'b000), .out(multiplexer_6_out),
    .sel(Choice));
  Multiplexer #(.select(5), .width(3)) multiplexer_7 (
    .in0(Instruction[5:3]), .in1(Instruction[5:3]), .in2(Instruction[5:3]), .in3(Instruction[5:3]),
    .in4(Instruction[5:3]), .in5(Instruction[5:3]), .in6(Instruction[5:3]), .in7(3'b000), .in8(3'b000),
    .in9(Instruction[10:8]), .in10(Instruction[10:8]), .in11(3'b000), .in12(3'b000), .in13(3'b000),
    .in14(3'b000), .in15(3'b000), .in16(3'b000), .in17(3'b000), .in18(3'b000), .in19(3'b000), .in20(3'b000),
    .in21(3'b000), .in22(3'b000), .in23(3'b000), .in24(3'b000), .in25(3'b000), .in26(3'b000), .in27(3'b000),
    .in28(3'b000), .in29(3'b000), .in30(3'b000), .in31(3'b000), .out(multiplexer_7_out), .sel(Choice));
  Multiplexer #(.select(5), .width(3)) multiplexer_8 (
    .in0(Instruction[10:8]), .in1(Instruction[10:8]), .in2(Instruction[10:8]), .in3(Instruction[10:8]),
    .in4(Instruction[10:8]), .in5(Instruction[10:8]), .in6(Instruction[10:8]), .in7(Instruction[2:0]),
    .in8(Instruction[2:0]), .in9(3'b000), .in10(3'b000), .in11(3'b000), .in12(3'b000), .in13(3'b000),
    .in14(3'b000), .in15(3'b000), .in16(3'b000), .in17(3'b000), .in18(3'b000), .in19(3'b000), .in20(3'b000),
    .in21(3'b000), .in22(3'b000), .in23(3'b000), .in24(3'b000), .in25(3'b000), .in26(3'b000), .in27(3'b000),
    .in28(3'b000), .in29(3'b000), .in30(3'b000), .in31(3'b000), .out(multiplexer_8_out), .sel(Choice));
  Multiplexer #(.select(5), .width(5)) multiplexer_9 (
    .in0(Instruction[10:6]), .in1(Instruction[10:6]), .in2(Instruction[10:6]), .in3({5{1'b0}}),
    .in4({5{1'b0}}), .in5({5{1'b0}}), .in6({5{1'b0}}), .in7({5{1'b0}}), .in8({5{1'b0}}), .in9({5{1'b0}}),
    .in10({5{1'b0}}), .in11({5{1'b0}}), .in12({5{1'b0}}), .in13({5{1'b0}}), .in14({5{1'b0}}),
    .in15({5{1'b0}}), .in16({5{1'b0}}), .in17({5{1'b0}}), .in18({5{1'b0}}), .in19({5{1'b0}}),
    .in20({5{1'b0}}), .in21({5{1'b0}}), .in22({5{1'b0}}), .in23({5{1'b0}}), .in24({5{1'b0}}),
    .in25({5{1'b0}}), .in26({5{1'b0}}), .in27({5{1'b0}}), .in28({5{1'b0}}), .in29({5{1'b0}}),
    .in30({5{1'b0}}), .in31({5{1'b0}}), .out(multiplexer_9_out), .sel(Choice));
  Multiplexer #(.width(32)) multiplexer_10 (.in0({32{1'b0}}), .in1(multiplexer_5_out), .out(Imm32), .sel(Enable));
  Multiplexer #(.width(3)) multiplexer_11 (.in0(3'b000), .in1(multiplexer_6_out), .out(Rm), .sel(Enable));
  Multiplexer #(.width(3)) multiplexer_12 (.in0(3'b000), .in1(multiplexer_7_out), .out(Rn), .sel(Enable));
  Multiplexer #(.width(3)) multiplexer_13 (.in0(3'b000), .in1(multiplexer_8_out), .out(Rd), .sel(Enable));
  Multiplexer #(.width(5)) multiplexer_14 (.in0({5{1'b0}}), .in1(multiplexer_9_out), .out(Imm5), .sel(Enable));

  // Other names for the same wires on the sheet: E = Enable; i[15:0] = Instruction; Imm8[7:0] = Instruction[7:0];
  //   Rd1[2:0] = Instruction[2:0]; Rm1_Rn[2:0] = Instruction[5:3]; Imm5_t[4:0] = Instruction[10:6];
  //   Rm2_Imm3[2:0] = Instruction[8:6]; Rd2_Rdn[2:0] = Instruction[10:8]

  // Notes on the sheet:
  //   Note 3: Imm32_Enable forces the use of the immediate for Rm register
  //   Pull output low on Enable = 0
  //   Enable carry for SUB since it is reversed in ALU
  //   Note: ALU uses Rn register for shifts. Use Rn instead of Rm for shifts (immediate) here too
  //   Note 2: MOV uses RSB ALU opcode with Imm8 reversed so that it is copied to output register
  //   only ADD and SUB use Rm
endmodule

module getter (
  input  [4:0] E,
  output [4:0] Choice,
  output [3:0] Codop,
  output [3:0] Flags
);

  wire and_1_out, and_2_out, and_3_out, and_4_out, and_5_out, and_6_out, and_7_out, and_8_out, and_9_out,
       and_10_out, and_11_out, and_12_out, and_13_out, and_15_out, and_16_out, and_17_out, and_18_out,
       and_19_out, and_20_out, and_21_out, and_22_out, and_23_out, and_24_out, and_25_out, and_26_out,
       and_27_out, and_28_out, not_1_out, not_2_out, not_3_out, not_4_out, not_5_out;

  not not_1 (not_1_out, E[4]);
  not not_2 (not_2_out, E[3]);
  not not_3 (not_3_out, E[2]);
  not not_4 (not_4_out, E[1]);
  not not_5 (not_5_out, E[0]);
  and and_1 (and_1_out, E[4], E[2]);
  and and_2 (and_2_out, E[4], E[3]);
  and and_3 (and_3_out, E[4], not_2_out, not_3_out);
  and and_4 (and_4_out, not_1_out, E[3], E[2], E[0]);
  and and_5 (and_5_out, not_1_out, E[3], E[2], E[1]);
  and and_6 (and_6_out, E[4], not_2_out, not_3_out);
  and and_7 (and_7_out, E[4], E[3], E[2]);
  and and_8 (and_8_out, not_1_out, E[3], not_3_out);
  and and_9 (and_9_out, not_1_out, E[3], not_4_out, not_5_out);
  and and_10 (and_10_out, not_1_out, E[3], E[1], E[0]);
  and and_11 (and_11_out, not_1_out, not_2_out, E[2]);
  and and_12 (and_12_out, not_1_out, E[2], not_5_out);
  and and_13 (and_13_out, E[4], not_3_out);
  and and_14 (Codop[3], E[4], not_2_out);
  and and_15 (and_15_out, E[4], not_3_out);
  and and_16 (and_16_out, E[2], E[0]);
  and and_17 (and_17_out, E[4], E[2]);
  and and_18 (and_18_out, E[4], not_3_out);
  and and_19 (and_19_out, not_1_out, E[2], not_5_out);
  and and_20 (and_20_out, not_1_out, not_2_out, E[2]);
  and and_21 (and_21_out, not_1_out, not_2_out);
  and and_22 (and_22_out, not_4_out, not_5_out);
  and and_23 (and_23_out, E[4], E[3]);
  and and_24 (and_24_out, not_1_out, not_4_out);
  and and_25 (and_25_out, E[4], not_4_out, not_5_out);
  and and_26 (and_26_out, E[4], E[2]);
  and and_27 (and_27_out, E[4], E[3]);
  and and_28 (and_28_out, E[3], E[2]);
  or or_1 (Choice[3], and_1_out, and_2_out);
  or or_2 (Choice[2], and_3_out, and_4_out, and_5_out);
  or or_3 (Choice[1], and_6_out, and_7_out, and_8_out, and_9_out, and_10_out);
  or or_4 (Choice[0], and_11_out, and_12_out, and_13_out);
  or or_5 (Codop[2], and_15_out, E[3]);
  or or_6 (Codop[1], not_2_out, and_16_out, and_17_out);
  or or_7 (Codop[0], and_18_out, and_19_out, and_20_out);
  or or_8 (Flags[1], and_21_out, E[2], and_22_out, and_23_out, and_24_out);
  or or_9 (Flags[0], and_25_out, and_26_out, and_27_out, and_28_out);

  assign Choice[4] = 1'b0;
  assign Flags[3:2] = 2'b11;
endmodule
